# Fritzing sketch OLED_Arduino_Uno (saved by Fritzing 0.9.3b)

parts:
  Grove2 = Grove OLED 128x96
  元件1 = Arduino Uno (Rev3)

nets:
  GND: Grove2.GND, 元件1.GND
  VCC: Grove2.VCC, 元件1.5V
  N1: Grove2.SDA, 元件1.A5/SCL
  N2: Grove2.SCL, 元件1.A4/SDA
