# Fritzing sketch OLED_Raspberry_Pi (saved by Fritzing 0.9.3b)

parts:
  Grove2 = Grove OLED 128x96
  Raspberry_Pi_1 = Raspberry Pi 3 [part_number=RPI-3-V1.2]

nets:
  GND: Grove2.GND, Raspberry_Pi_1.GND
  VCC: Grove2.VCC, Raspberry_Pi_1.5V
  N1: Grove2.SDA, Raspberry_Pi_1.GPIO2
  N2: Grove2.SCL, Raspberry_Pi_1.GPIO3
